# Fritzing sketch ceres (saved by Fritzing 0.9.3b)
breadboards: 1

parts:
  J1 = Infrared Proximity Sensor  # not connected
  Part1 = Arduino Uno (Rev3)
  LCD1 = LCD screen
  L1 = Solenoid  # not connected
  VCC1 = Battery  # not connected
  U1 = RELAY-SOLIDSTATE [package=relay-s108t02]
  S1 = SWITCH-MOMENTARY-2 [package=tactile-pth-12mm]  # not connected
  S2 = SWITCH-MOMENTARY-2 [package=tactile-pth-12mm]  # not connected
  S3 = Square Pushbutton  # not connected
  S4 = SWITCH-MOMENTARY-2 [package=tactile-pth-12mm]  # not connected
  LED1 = smd LED [color="Blue (505nm)" package="0603 [SMD]"]  # not connected
  S5 = SPST Switch [package=switche-dpdt]  # not connected
  S6 = Round Pushbutton  # not connected
  LCD2 = LCD screen  # not connected
  LED2 = smd LED [color="Red (660nm)" package="0603 [SMD]"]  # not connected
  Part2 = NCP1400 Step-Up Breakout  # not connected
  L2 = Solenoid  # not connected
  U2 = RELAY-2 [package=relay-g5v]  # not connected

nets:
  N1: Part1.A4/SDA, LCD1.V0
  N2: Part1.A5/SCL, LCD1.RS
  5V: Part1.5V, LCD1.VDD, U1.-
  GND: Part1.GND, LCD1.VSS, U1.T2

notes:
  Flow Sensor
  Tank Drain Solenoid
  Set
  DOWN
  UP
  ENTER
  FLOOD
  DRAIN
  Set-up 12 V Regulator
  Turn off water solenoid
